# Fritzing sketch barrier (saved by Fritzing 0.9.3b)
breadboards: 1

parts:
  U1 = NodeMCU V1.0
  TCRT2 = TCRT5000 digital module [part_number=151608]

nets:
  N1: U1.D1, TCRT2.DO1
  3V3: U1.3V3, TCRT2.VCC
  GND: U1.GND, TCRT2.GND

custom parts:
  NodeMCU V1.0: ESP8266 based NodeMCU
  TCRT5000 digital module: breakout board for TCRT5000 module, convert analog to digital - Uses TCRT5000 infrared reflectance sensor - Detection distance: 1mm~8mm - Focus distance: 2.5mm - Working voltage: 3.3V~12V - Uses wide voltage LM393 comparator - With multi-turn precision potentiometer to adjust the sensitivity - Current: > 15mA - Output type: Digital switch output (0, 1) - Suitable for watt-hour meter pulse data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
